// Logisim project control-logic.circ as structural Verilog: 1 circuit, main circuit control_logic
module control_logic (
  input  [31:0] Instruction,
  input  BrEq,
  input  BrLt,
  output PCSel,
  output RegWEn,
  output [2:0] ImmSel,
  output BrUn,
  output ASel,
  output BSel,
  output [3:0] ALUSel,
  output MemWEn,
  output [1:0] WBSel
);

  wire comparator_1_eq, comparator_2_eq, comparator_3_eq, comparator_4_eq, comparator_16_eq,
       comparator_17_eq, is_add, is_addi, is_and, is_lb, is_lh, is_lw, is_mul, is_mulh, is_mulhu, is_or,
       is_sll, is_slt, is_sra, is_srl, is_sub, is_xor;
  wire [2:0] bit_extender_2_out, bit_extender_3_out, fun3_or0_I1, fun3_or0_I2;
  wire [5:0] ROM_input;
  wire [9:0] bit_extender_1_out, fun3fun7;
  wire [15:14] rom_1_data;

  assign bit_extender_1_out = {{9{comparator_1_eq}}, comparator_1_eq};  // Bit_Extender bit_extender_1
  Comparator #(.width(7)) comparator_1 (.a(7'b0110011), .b(Instruction[6:0]), .eq(comparator_1_eq));  // open: gt, lt
  Comparator #(.width(7)) comparator_2 (.a(7'b0010011), .b(Instruction[6:0]), .eq(comparator_2_eq));  // open: gt, lt
  assign bit_extender_2_out = {{2{comparator_3_eq}}, comparator_3_eq};  // Bit_Extender bit_extender_2
  Comparator #(.width(7)) comparator_3 (.a(7'b0000011), .b(Instruction[6:0]), .eq(comparator_3_eq));  // open: gt, lt
  assign fun3fun7 = bit_extender_1_out & {Instruction[14:12], Instruction[31:25]};  // AND_Gate and_1, 10 bits wide
  assign bit_extender_3_out = {{2{comparator_2_eq}}, comparator_2_eq};  // Bit_Extender bit_extender_3
  assign fun3_or0_I2 = bit_extender_2_out & Instruction[14:12];  // AND_Gate and_2, 3 bits wide
  ROM #(.addrWidth(6), .dataWidth(16)) rom_1 (
    .addr(ROM_input), .data({rom_1_data, WBSel, MemWEn, ALUSel, BSel, ASel, BrUn, ImmSel, RegWEn}));
  assign fun3_or0_I1 = bit_extender_3_out & Instruction[14:12];  // AND_Gate and_3, 3 bits wide
  Comparator #(.width(10)) comparator_4 (.a(fun3fun7), .b({10{1'b0}}), .eq(comparator_4_eq));  // open: gt, lt
  Comparator #(.width(10)) comparator_5 (.a(fun3fun7), .b(10'h1), .eq(is_mul));  // open: gt, lt
  Comparator #(.width(10)) comparator_6 (.a(fun3fun7), .b(10'h20), .eq(is_sub));  // open: gt, lt
  Comparator #(.width(10)) comparator_7 (.a(fun3fun7), .b(10'h80), .eq(is_sll));  // open: gt, lt
  Comparator #(.width(10)) comparator_8 (.a(fun3fun7), .b(10'h81), .eq(is_mulh));  // open: gt, lt
  Comparator #(.width(10)) comparator_9 (.a(fun3fun7), .b(10'h181), .eq(is_mulhu));  // open: gt, lt
  Comparator #(.width(10)) comparator_10 (.a(fun3fun7), .b(10'h100), .eq(is_slt));  // open: gt, lt
  Comparator #(.width(10)) comparator_11 (.a(fun3fun7), .b(10'h200), .eq(is_xor));  // open: gt, lt
  Comparator #(.width(10)) comparator_12 (.a(fun3fun7), .b(10'h280), .eq(is_srl));  // open: gt, lt
  Comparator #(.width(10)) comparator_13 (.a(fun3fun7), .b(10'h2a0), .eq(is_sra));  // open: gt, lt
  Comparator #(.width(10)) comparator_14 (.a(fun3fun7), .b(10'h300), .eq(is_or));  // open: gt, lt
  Comparator #(.width(10)) comparator_15 (.a(fun3fun7), .b(10'h380), .eq(is_and));  // open: gt, lt
  and and_4 (is_add, comparator_4_eq, comparator_1_eq);
  Comparator #(.width(3)) comparator_16 (.a(fun3_or0_I1), .b(3'b000), .eq(comparator_16_eq));  // open: gt, lt
  Comparator #(.width(3)) comparator_17 (.a(fun3_or0_I2), .b(3'b000), .eq(comparator_17_eq));  // open: gt, lt
  Comparator #(.width(3)) comparator_18 (.a(fun3_or0_I2), .b(3'b001), .eq(is_lh));  // open: gt, lt
  Comparator #(.width(3)) comparator_19 (.a(fun3_or0_I2), .b(3'b010), .eq(is_lw));  // open: gt, lt
  and and_5 (is_addi, comparator_2_eq, comparator_16_eq);
  and and_6 (is_lb, comparator_3_eq, comparator_17_eq);
  // Priority_Encoder #(.select_enc(6)) priority_encoder_1: pin names not known; wires that end beside it: ROM_input, is_add, is_mul, is_sub, is_sll, is_mulh, is_mulhu, is_slt, is_xor, is_srl, is_sra, is_or, is_and, is_lb, is_lh, is_lw, is_addi

  assign PCSel = 1'b0;

  // Other names for the same wires on the sheet: fun7[6:0] = Instruction[31:25]; fun3[2:0] = Instruction[14:12];
  //   Opcode[6:0] = Instruction[6:0]

  // Notes on the sheet:
  //   INPUTS to your circuit
  //   contents of rom_1 (hex, n*v repeats v):
  //   1 401 601 81 481 581 101 201 281 681 301 381 1041 1041 1041 41
  //   ROM FOR CONTROL LOGIC
  //   DON'T CHANGE THE LOCATIONS OF THE INPUTS AND OUTPUTS!
  //   This is only if you choose to do the ROM option
  //   CONNECT
  //   WIRE
  //   TO
  //   USE
  //   ROM
  //   OUTPUT from your circuit
  //   Reminder: If using ROM, use combinational logic for PCSel
endmodule
