// Logisim project regfile.circ as structural Verilog: 1 circuit, main circuit regfile
module regfile (
  input  [4:0] ReadIndex1,
  input  [4:0] ReadIndex2,
  input  [4:0] WriteIndex,
  input  [31:0] WriteData,
  input  RegWEn,
  input  clk,
  output [31:0] ra,
  output [31:0] sp,
  output [31:0] t0,
  output [31:0] t1,
  output [31:0] t2,
  output [31:0] s0,
  output [31:0] s1,
  output [31:0] a0,
  output [31:0] ReadData1,
  output [31:0] ReadData2
);

  wire [31:0] demultiplexer_1_out0, demultiplexer_1_out18, demultiplexer_1_out19, x0, x1D, x2D, x3D, x3Q,
       x4D, x4Q, x5D, x6D, x7D, x8D, x9D, x10D, x11D, X11Q, x11Q_t, x12D, X12Q, x12Q_t, x13D, x13Q, x14D,
       x14Q, x15D, x15Q, x16D, x16Q, x17D, x17Q, x18D, x18Q, x19D, x19Q, x20D, x20Q, x21Q, x22Q, x23D, x23Q,
       x24D, x24Q, x25D, x25Q, x26D, x26Q, x27D, x27Q, x28D, x28Q, x29D, x29Q, x30D, x30Q, x31D, x31Q;

  Demultiplexer #(.select(5), .width(32)) demultiplexer_1 (
    .out0(demultiplexer_1_out0), .out1(x1D), .out2(x2D), .out5(x5D), .out6(x6D), .out7(x7D), .out8(x8D),
    .out9(x9D), .out10(x10D), .out11(x11D), .out12(x12D), .out13(x13D), .out14(x14D), .out15(x15D),
    .out16(x16D), .out17(x17D), .out18(demultiplexer_1_out18), .out19(demultiplexer_1_out19), .out20(x18D),
    .out21(x20D), .out22(x19D), .out23(x23D), .out24(x24D), .out25(x25D), .out26(x26D), .out27(x27D),
    .out28(x28D), .out29(x29D), .out30(x30D), .out31(x31D), .in(WriteData), .sel(WriteIndex));  // open: out3, out4
  Register #(.width(32)) x28 (.D(x28D), .en(RegWEn), .Q(x28Q), .clr(clk));  // open: clk
  Register #(.width(32)) x29 (.D(x29D), .en(RegWEn), .Q(x29Q), .clr(clk));  // open: clk
  Register #(.width(32)) x30 (.D(x30D), .en(RegWEn), .Q(x30Q), .clr(clk));  // open: clk
  Register #(.width(32)) x31 (.D(x31D), .en(RegWEn), .Q(x31Q), .clr(clk));  // open: clk
  Register #(.width(32)) register_1 (.D({32{1'b0}}), .Q(x0), .clr(clk));  // open: en, clk
  Register #(.width(32)) x16 (.D(x16D), .en(RegWEn), .Q(x16Q), .clr(clk));  // open: clk
  Register #(.width(32)) x17 (.D(x17D), .en(RegWEn), .Q(x17Q), .clr(clk));  // open: clk
  Register #(.width(32)) x18 (.D(x18D), .en(RegWEn), .Q(x18Q), .clr(clk));  // open: clk
  Register #(.width(32)) x19 (.D(x19D), .en(RegWEn), .Q(x19Q), .clr(clk));  // open: clk
  Register #(.width(32)) x20 (.D(x20D), .en(RegWEn), .Q(x20Q), .clr(clk));  // open: clk
  Register #(.width(32)) x21 (.D(x20D), .en(RegWEn), .Q(x21Q), .clr(clk));  // open: clk
  Register #(.width(32)) x22 (.D(x19D), .en(RegWEn), .Q(x22Q), .clr(clk));  // open: clk
  Register #(.width(32)) x23 (.D(x23D), .en(RegWEn), .Q(x23Q), .clr(clk));  // open: clk
  Register #(.width(32)) x24 (.D(x24D), .en(RegWEn), .Q(x24Q), .clr(clk));  // open: clk
  Register #(.width(32)) x25 (.D(x25D), .en(RegWEn), .Q(x25Q), .clr(clk));  // open: clk
  Register #(.width(32)) x26 (.D(x26D), .en(RegWEn), .Q(x26Q), .clr(clk));  // open: clk
  Register #(.width(32)) x27 (.D(x27D), .en(RegWEn), .Q(x27Q), .clr(clk));  // open: clk
  Register #(.width(32)) x1 (.D(x1D), .en(RegWEn), .Q(ra), .clr(clk));  // open: clk
  Register #(.width(32)) x2 (.D(x2D), .en(RegWEn), .Q(sp), .clr(clk));  // open: clk
  Register #(.width(32)) x5 (.D(x5D), .en(RegWEn), .Q(t0), .clr(clk));  // open: clk
  Register #(.width(32)) x6 (.D(x6D), .en(RegWEn), .Q(t1), .clr(clk));  // open: clk
  Register #(.width(32)) x7 (.D(x7D), .en(RegWEn), .Q(t2), .clr(clk));  // open: clk
  Register #(.width(32)) x8 (.D(x8D), .en(RegWEn), .Q(s0), .clr(clk));  // open: clk
  Register #(.width(32)) x9 (.D(x9D), .en(RegWEn), .Q(s1), .clr(clk));  // open: clk
  Register #(.width(32)) x10 (.D(x10D), .en(RegWEn), .Q(a0), .clr(clk));  // open: clk
  Register #(.width(32)) x3 (.D(x3D), .en(RegWEn), .Q(x3Q), .clr(clk));  // open: clk
  Register #(.width(32)) x4 (.D(x4D), .en(RegWEn), .Q(x4Q), .clr(clk));  // open: clk
  Register #(.width(32)) x11 (.D(x11D), .en(RegWEn), .Q(x11Q_t), .clr(clk));  // open: clk
  Register #(.width(32)) x12 (.D(x12D), .en(RegWEn), .Q(x12Q_t), .clr(clk));  // open: clk
  Register #(.width(32)) x13 (.D(x13D), .en(RegWEn), .Q(x13Q), .clr(clk));  // open: clk
  Register #(.width(32)) x14 (.D(x14D), .en(RegWEn), .Q(x14Q), .clr(clk));  // open: clk
  Register #(.width(32)) x15 (.D(x15D), .en(RegWEn), .Q(x15Q), .clr(clk));  // open: clk
  Multiplexer #(.select(5), .width(32)) multiplexer_1 (
    .in0(x0), .in1(ra), .in2(sp), .in3(x3Q), .in4(x4Q), .in5(t0), .in6(t1), .in7(t2), .in8(s0), .in9(s1),
    .in10(a0), .in11(X11Q), .in12(X12Q), .in13(x13Q), .in14(x14Q), .in15(x15Q), .in16(x16Q), .in17(x17Q),
    .in18(x18Q), .in19(x19Q), .in20(x20Q), .in21(x21Q), .in22(x22Q), .in23(x23Q), .in24(x24Q), .in25(x25Q),
    .in26(x26Q), .in27(x27Q), .in28(x28Q), .in29(x29Q), .in30(x30Q), .in31(x31Q), .out(ReadData1),
    .sel(ReadIndex1));
  Multiplexer #(.select(5), .width(32)) multiplexer_2 (
    .in0(x0), .in1(ra), .in2(sp), .in3(x3Q), .in4(x4Q), .in5(t0), .in6(t1), .in7(t2), .in8(s0), .in9(s1),
    .in10(a0), .in11(X11Q), .in12(X12Q), .in13(x13Q), .in14(x14Q), .in15(x15Q), .in16(x16Q), .in17(x17Q),
    .in18(x18Q), .in19(x19Q), .in20(x20Q), .in21(x21Q), .in22(x22Q), .in23(x23Q), .in24(x24Q), .in25(x25Q),
    .in26(x26Q), .in27(x27Q), .in28(x28Q), .in29(x29Q), .in30(x30Q), .in31(x31Q), .out(ReadData2),
    .sel(ReadIndex2));

  // Other names for the same wires on the sheet: X1Q[31:0] = ra; X2Q[31:0] = sp; X5Q[31:0] = t0; X6Q[31:0] = t1;
  //   X7Q[31:0] = t2; X8Q[31:0] = s0; X9Q[31:0] = s1; X10Q[31:0] = a0; x21D[31:0] = x20D; x22D[31:0] = x19D

  // Notes on the sheet:
  //   INPUTS to your circuit
  //   DON'T CHANGE THE LOCATIONS OF THE INPUTS AND OUTPUTS!
  //   These are DEBUG/TEST outputs from your circuit.
  //   OUTPUTS from your circuit
endmodule
